# Fritzing sketch Rangkaian (saved by Fritzing 0.9.3b)
breadboards: 1

parts:
  EPP32 = MH-ET LIVE ESP32 DEVKIT 38 pins
  part = LCD2004-I2C
  J1 = Basic Servo
  part_2 = LJ18A3-H-ZBX [package=THT]
  Keypad4x1 = Keypad Membran 4x4
  part_3 = HC-SR04 Ultrasonic Distance Sensor
  Mod3 = ESP32 - CAM
  VCC1 = 4 x AAA Battery Mount

nets:
  N1: EPP32.IO32, Keypad4x1.Pin6
  N2: EPP32.IO33, Keypad4x1.Pin7
  N3: EPP32.IO25, Keypad4x1.Pin1
  N4: EPP32.IO26, Keypad4x1.Pin2
  N5: EPP32.IO27, Keypad4x1.Pin3
  N6: EPP32.IO12, J1.pulse
  GND: EPP32.GND, part.GND, J1.gnd, part_2.VO_(BLU), part_3.GND
  N7: EPP32.IO13, Keypad4x1.Pin5
  VCC: EPP32.5V, part.VCC, J1.vcc, part_2.VI_(BRN), part_3.VCC
  N8: EPP32.IO23, Keypad4x1.Pin8
  N9: EPP32.IO22, part.SCL
  N10: EPP32.IO21, part.SDA
  N11: EPP32.IO18, part_3.ECHO
  N12: EPP32.IO5, part_3.TRIG
  N13: EPP32.IO2, part_2.SIG_(BLK)
  N14: EPP32.IO15, Keypad4x1.Pin4
  N15: Mod3.5V, VCC1.+
  N16: Mod3.GND, VCC1.-

custom parts:
  MH-ET LIVE ESP32 DEVKIT 38 pins: http://mh.nodebb.com/topic/2/mh-et-live-esp32-devkit
  LCD2004-I2C: A standard character display with 4x20 characters. Comes in many colors with LCM2004 IIC attached.
  LJ18A3-H-ZBX: LJ18A3-H-ZBX Proximity Sensor module.
  Keypad Membran 4x4: Membrane Keypad 4x4 Matrix
  HC-SR04 Ultrasonic Distance Sensor: The HC-SR04 is an ultrasonic distance sensor. It is capable of providing measurement for ranges of 2cm to 400cm. The module operates at 5V.
  ESP32 - CAM: The ESP32-CAM has a very competitive small-size camera module that can operate independently as a minimum system with a footprint of only 27*40.5*4.5mm and a deep sleep current of up to 6mA.
